# Fritzing sketch UselessBoxes (saved by Fritzing 1.0.5)
circuit board: 8.46667cm x 5.64444cm
breadboards: 1

parts:
  S1 = Toggle Switch [package=THT]
  M1 = DC Motor [voltage_(max)=6V voltage_(min)=3V]
  Power_plug1 = Power plug
  IC1 = H-Bridge [package=THT]
  S2 = SPST Switch [package=switch-spdt_kit]
  Part1 = Arduino Nano (Rev3.0)
  R1 = Resistor [tolerance=±5% power=0.25W resistance=10k package=THT]
  R2 = Resistor [tolerance=±5% power=0.25W resistance=10k package=THT]

nets:
  N1: S1.COM, S2.O, Part1.3V3
  N2: S1.L2, Part1.D6, R2.Pin_0
  N3: M1.pin_1, IC1.2Y
  N4: M1.pin_2, IC1.1Y
  GND: Power_plug1.GND, IC1.GND4, Part1.GND, R1.Pin_1, R2.Pin_1
  N5: Power_plug1.VCC, IC1.VCC2, IC1.VCC1
  N6: IC1.1_2EN, Part1.D4
  N7: IC1.1A, Part1.D3
  N8: IC1.2A, Part1.D2
  N9: S2.P, Part1.D7, R1.Pin_0
